# Fritzing sketch KnockSensorSketch (saved by Fritzing 0.6.3b)
breadboards: 1

parts:
  Netduino1 = Netduino
  R1 = Resistor [tolerance=±5% resistance=220 package=THT]
  J1 = Piezo Speaker

nets:
  N1: Netduino1.GND, R1.Pin_0, R1.Pin_1, J1.pin1, J1.pin2
