# Fritzing sketch photocellschematic (saved by Fritzing 0.6.3b)
breadboards: 1

parts:
  Netduino1 = Netduino
  R1 = Resistor [tolerance=±5% resistance=220 package=THT]
  R2 = Photocell (LDR) [package=THT]
  LED1 = LED - 5mm [color="Red (633nm)" package="5 mm [THT]"]
  LED2 = LED - 5mm [color="Red (633nm)" package="5 mm [THT]"]

nets:
  N1: Netduino1.D10_PWM3, LED1.cathode
  N2: Netduino1.D7_RTS1, LED2.cathode
  N3: Netduino1.GND, R2.pin_0
  N4: Netduino1.A0, R1.Pin_1
  N5: R1.Pin_0, R2.pin_1
  N6: LED1.anode, LED2.anode
